# Fritzing sketch RGBWithArduinoWithPotentiometers (saved by Fritzing 0.9.0b)
breadboards: 1

parts:
  LED1 = RGB LED (com. cathode, rgb) [package="5 mm [THT]"]
  R1 = TRIMPOT [package=3386u]
  R2 = TRIMPOT [package=3386u]
  R3 = TRIMPOT [package=3386u]
  R4 = Resistor [tolerance=±5% resistance=220 package="1206 [SMD]"]
  R5 = Resistor [tolerance=±5% resistance=220 package="1206 [SMD]"]
  R6 = Resistor [tolerance=±5% resistance=220 package="1206 [SMD]"]
  Part1 = Arduino Uno (Rev3)

nets:
  N1: LED1.red_anode, R4.Pin_1
  N2: LED1.common_cathode, R1.CCW, R2.CCW, R3.CCW, R5.Pin_1, Part1.GND
  N3: LED1.blue_anode, R6.Pin_1
  N4: R1.WIPER, Part1.A0
  N5: R1.CW, R2.CW, R3.CW
  N6: R2.WIPER, Part1.A1
  N7: R3.WIPER, Part1.A2
  N8: R4.Pin_0, Part1.D3_PWM
  N9: R5.Pin_0, Part1.D5_PWM
  N10: R6.Pin_0, Part1.D7

notes:
  Red
  GND
  Potentiometers: 10K
  Resistors: 220 Ohms
  With Arduino
  Blue
  Green
